# Fritzing sketch HenHouse (saved by Fritzing 0.9.9b)

parts:
  Composant1 = Adafruit USB DC Solar LiPo Charger [part_number="Adafruit #390"]
  Composant2 = Lithium Ion Battery Pack 3.7V 4400mAh [part_number=354]  # not connected
  U1 = DC-DC_CONVERTER [package=dc-dc_converter]  # not connected
  D1 = SOLAR-IXYS [package=solarbit-12x1]  # not connected
  M1 = DC Motor
  DS1 = DS18B20 1-Wire Temperature Sensor [part_number=DS18B20]
  DS2 = DS18B20 1-Wire Temperature Sensor [part_number=DS18B20]  # not connected
  DS3 = DS18B20 1-Wire Temperature Sensor [part_number=DS18B20]  # not connected
  DS4 = DS18B20 1-Wire Temperature Sensor [part_number=DS18B20]
  R2 = Resistor [tolerance=±5% resistance=3.3k package="0603 [SMD]"]
  Composant4 = Motor Driver 1A Dual TB6612FNG
  S3 = Pushbutton [package="[THT]"]
  S4 = Pushbutton [package="[THT]"]
  R4 = Resistor [tolerance=±5% resistance=3.3k package="0603 [SMD]"]  # not connected
  R5 = Resistor [tolerance=±5% resistance=3.3k package="0603 [SMD]"]
  R6 = Resistor [tolerance=±5% resistance=3.3k package="0603 [SMD]"]  # not connected
  R7 = Resistor [tolerance=±5% resistance=3.3k package="0603 [SMD]"]
  Composant5 = Adafruit Feather M0 RFM9x LoRa [part_number="Adafruit #3178 or #3179"]
  S5 = SWITCH-MOMENTARY-2 [package=reed_switch_pth]  # not connected
  S6 = SWITCH-MOMENTARY-2 [package=reed_switch_pth]  # not connected

nets:
  N1: Composant1.CHARGE, Composant5.D11
  N2: Composant1.DONE, Composant5.D12
  N3: M1.pin_1, Composant4.A02
  N4: M1.pin_2, Composant4.A01
  N5: DS1.DQ, Composant5.A4
  VDD: DS1.VDD, R2.Pin_1, Composant5.+3V3
  N6: DS4.DQ, R2.Pin_0
  N7: Composant4.AIN2, Composant5.A2
  N8: Composant4.AIN1, Composant5.A3
  N9: Composant4.STBY, Composant5.A5
  N10: S3.Pin_1, S3.Pin_2, Composant5.D0
  N11: S3.Pin_4, S4.Pin_3, S4.Pin_4
  N12: S4.Pin_1, S4.Pin_2, Composant5.D1
  N13: R5.Pin_1, Composant5.A1
  N14: R7.Pin_0, Composant5.A0
  N15: Composant5.DIO1, Composant5.D6

custom parts:
  Adafruit USB DC Solar LiPo Charger: Make your projects to go green this summer with our specialized USB/Solar Lithium Ion Polymer Battery charger! This charger is a very unique design, perfect for outdoor projects, or DIY iPod chargers. We've spent over a year testing and tinkering with this charger to come up with a plug and play solution to charging batteries with the sun and we're really pleased with what we ended up with.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
  Lithium Ion Battery Pack 3.7V 4400mAh: This lithium ion pack is made of 2 balanced 2200mAh cells for a total of 4400mA capacity! The cells are connected in parallel and spot-welded to a protection circuit that provides over-voltage, under-voltage and over-current protection. Each cell can provide 1A of current for about 4 hours so all together the peak current you can draw is a little over 1.5 Amps. Note that these batteries are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
  Adafruit Feather M0 RFM9x LoRa: This is the Adafruit Feather M0 RFM95 LoRa Radio - our take on an microcontroller with a "Long Range (LoRa)" packet radio transceiver with built in USB and battery charging. Its an Adafruit Feather M0 with a 433Mhz or 900MHz radio module cooked in! Great for making wireless networks that are more flexible than Bluetooth LE and without the high power requirements of WiFi. We have other boards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
